# Fritzing sketch IF-N80K-ESP32 (saved by Fritzing 0.9.5d)
breadboards: 1

parts:
  esp1 = ESP32 DevKitc V4
  M1 = E18-D80NK_1 [package=THT]
  BAT1 = BC9VPC [package=bc9vpc]
  R1 = Resistor [tolerance=±5% resistance=220 package="1206 [SMD]"]

nets:
  N1: esp1.IO26, M1.pin3
  N2: esp1.5V, M1.pin2, R1.Pin_0
  N3: M1.pin1, BAT1.V-
  N4: BAT1.V+, R1.Pin_1

custom parts:
  ESP32 DevKitc V4: ESP32-DevKitC board with ESP32-WROOM-32 module. ESP32-DevKitC V4 is a small-sized ESP32-based development board produced by Espressif. Most of the pins on the ESP module are broken out to the pin headers on the board. The pins D0, D1, D2, D3, CMD and CLK are used internally for communication between ESP32 and SPI flash memory. They are grouped on both sides near the USB connector. Avoid using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
  E18-D80NK_1: E18-D80NK Proximity Sensor module.
