# Fritzing sketch Stopwatch Run IOT (saved by Fritzing 0.9.5d)

parts:
  esp1 = ESP32 DevKitc V4
  Part2 = LCD1602-I2C
  M1 = 1 chan 5v relay module
  U1 = LM2596 step down module
  J1 = Piezo Speaker
  S1 = Round Pushbutton

nets:
  N1: esp1.IO25, S1.leg0
  N2: esp1.IO27, M1.pin_3
  N3: esp1.D2, Part2.SDA
  N4: esp1.D1, Part2.SCL
  N5: M1.pin_1, U1.OUT+
  N6: M1.pin_2, U1.IN-, U1.OUT-
  N7: M1.pin_5, J1.pin2

custom parts:
  ESP32 DevKitc V4: ESP32-DevKitC board with ESP32-WROOM-32 module. ESP32-DevKitC V4 is a small-sized ESP32-based development board produced by Espressif. Most of the pins on the ESP module are broken out to the pin headers on the board. The pins D0, D1, D2, D3, CMD and CLK are used internally for communication between ESP32 and SPI flash memory. They are grouped on both sides near the USB connector. Avoid using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
  LCD1602-I2C: A standard character display, usually with 2x16 characters. Comes in many colors with LCM1602 IIC attached.
  1 chan 5v relay module: 1 Channel 5V Relay Module Board Shield with Optocoupler Support High and Low Level Trigger for Arduino.
  LM2596 step down module: LM2596 DC-DC step down power supply module 3 A.
